// Logisim project ex3.circ as structural Verilog: 1 circuit, main circuit non_pipelined
module non_pipelined (
  input  [7:0] in1,
  input  [7:0] in2,
  input  CLK,
  output [7:0] out1
);

  wire [7:0] adder_1_out, multiplier_1_out, register_1_q;

  Register register_1 (.D(multiplier_1_out), .clk(CLK), .Q(register_1_q));  // open: en, clr
  Multiplier multiplier_1 (.a(in1), .b(in2), .out(multiplier_1_out));  // open: cin, cout
  Register register_2 (.D(adder_1_out), .clk(CLK), .Q(out1));  // open: en, clr
  Adder adder_1 (.a(register_1_q), .b(out1), .out(adder_1_out));  // open: cin, cout
endmodule
