// Logisim project control-logic.circ as structural Verilog: 1 circuit, main circuit control_logic
module control_logic (
  input  [31:0] Instruction,
  input  BrEq,
  input  BrLt,
  output PCSel,
  output RegWEn,
  output [2:0] ImmSel,
  output BrUn,
  output ASel,
  output BSel,
  output [3:0] ALUSel,
  output MemWEn,
  output [1:0] WBSel
);

  wire add0, addi15, and11, and_1_out, and_2_out, and_3_out, and_4_out, and_5_out, and_6_out, andi22,
       auipc32, beq26, bge29, bgeu31, blt28, bltu30, bne27, comparator_23_eq, comparator_34_eq,
       comparator_35_eq, comparator_36_eq, comparator_37_eq, comparator_38_eq, comparator_39_eq,
       comparator_40_eq, jal34, jalr35, lb12, lh13, lui33, lw14, mul1, mulh4, mulhu5, not_1_out, not_2_out,
       not_3_out, or10, ori21, sb23, sh24, sll3, slli16, slt6, slti17, sra9, srai20, srl8, srli19, sub2,
       sw25, XOR7, xori18;
  wire [0:0] comparator_1_eq, comparator_2_gt, comparator_3_eq, comparator_4_eq, comparator_5_eq,
       comparator_9_eq, comparator_19_eq, comparator_22_eq, comparator_24_eq, comparator_41_eq,
       comparator_42_eq, comparator_46_eq;
  wire [5:0] Address;
  wire [15:14] rom_1_data;

  Comparator #(.mode("unsigned"), .width(7)) comparator_1 (
    .a(Instruction[6:0]), .b(7'b0110011), .eq(comparator_1_eq[0]));  // open: gt, lt
  ROM #(.addrWidth(6), .dataWidth(16)) rom_1 (
    .addr(Address), .data({rom_1_data, WBSel, MemWEn, ALUSel, BSel, ASel, BrUn, ImmSel, RegWEn}));
  Comparator #(.mode("unsigned"), .width(7)) comparator_2 (
    .a(Instruction[6:0]), .b(7'b0000011), .gt(comparator_2_gt[0]), .eq(comparator_2_gt[0]),
    .lt(comparator_2_gt[0]));
  Comparator #(.mode("unsigned"), .width(7)) comparator_3 (
    .a(Instruction[6:0]), .b(7'b0010011), .eq(comparator_3_eq[0]));  // open: gt, lt
  Comparator #(.mode("unsigned"), .width(4)) comparator_4 (
    .a({Instruction[14:12], comparator_1_eq[0]}), .b(4'b0001), .eq(comparator_4_eq[0]));  // open: gt, lt
  Comparator #(.mode("unsigned"), .width(4)) comparator_5 (
    .a({Instruction[14:12], comparator_1_eq[0]}), .b(4'b0011), .eq(comparator_5_eq[0]));  // open: gt, lt
  Comparator #(.mode("unsigned"), .width(4)) comparator_6 (
    .a({Instruction[14:12], comparator_1_eq[0]}), .b(4'b0111), .eq(mulhu5));  // open: gt, lt
  Comparator #(.mode("unsigned"), .width(4)) comparator_7 (
    .a({Instruction[14:12], comparator_1_eq[0]}), .b(4'b0101), .eq(slt6));  // open: gt, lt
  Comparator #(.mode("unsigned"), .width(4)) comparator_8 (
    .a({Instruction[14:12], comparator_1_eq[0]}), .b(4'b1001), .eq(XOR7));  // open: gt, lt
  Comparator #(.mode("unsigned"), .width(4)) comparator_9 (
    .a({Instruction[14:12], comparator_1_eq[0]}), .b(4'b1011), .eq(comparator_9_eq[0]));  // open: gt, lt
  Comparator #(.mode("unsigned"), .width(4)) comparator_10 (
    .a({Instruction[14:12], comparator_1_eq[0]}), .b(4'b1101), .eq(or10));  // open: gt, lt
  Comparator #(.mode("unsigned"), .width(4)) comparator_11 (
    .a({Instruction[14:12], comparator_1_eq[0]}), .b(4'b1111), .eq(and11));  // open: gt, lt
  Comparator #(.mode("unsigned"), .width(4)) comparator_12 (
    .a({Instruction[14:12], comparator_2_gt[0]}), .b(4'b0001), .eq(lb12));  // open: gt, lt
  Comparator #(.mode("unsigned"), .width(4)) comparator_13 (
    .a({Instruction[14:12], comparator_2_gt[0]}), .b(4'b0011), .eq(lh13));  // open: gt, lt
  Comparator #(.mode("unsigned"), .width(4)) comparator_14 (
    .a({Instruction[14:12], comparator_2_gt[0]}), .b(4'b0101), .eq(lw14));  // open: gt, lt
  Comparator #(.mode("unsigned"), .width(4)) comparator_15 (
    .a({Instruction[14:12], comparator_3_eq[0]}), .b(4'b0001), .eq(addi15));  // open: gt, lt
  Comparator #(.mode("unsigned"), .width(4)) comparator_16 (
    .a({Instruction[14:12], comparator_3_eq[0]}), .b(4'b0011), .eq(slli16));  // open: gt, lt
  Comparator #(.mode("unsigned"), .width(4)) comparator_17 (
    .a({Instruction[14:12], comparator_3_eq[0]}), .b(4'b0101), .eq(slti17));  // open: gt, lt
  Comparator #(.mode("unsigned"), .width(4)) comparator_18 (
    .a({Instruction[14:12], comparator_3_eq[0]}), .b(4'b1001), .eq(xori18));  // open: gt, lt
  Comparator #(.mode("unsigned"), .width(4)) comparator_19 (
    .a({Instruction[14:12], comparator_3_eq[0]}), .b(4'b1011), .eq(comparator_19_eq[0]));  // open: gt, lt
  Comparator #(.mode("unsigned"), .width(4)) comparator_20 (
    .a({Instruction[14:12], comparator_3_eq[0]}), .b(4'b1101), .eq(ori21));  // open: gt, lt
  Comparator #(.mode("unsigned"), .width(4)) comparator_21 (
    .a({Instruction[14:12], comparator_3_eq[0]}), .b(4'b1111), .eq(andi22));  // open: gt, lt
  Comparator #(.mode("unsigned"), .width(7)) comparator_22 (
    .a(Instruction[6:0]), .b(7'b1100011), .eq(comparator_22_eq[0]));  // open: gt, lt
  Comparator #(.mode("unsigned"), .width(7)) comparator_23 (
    .a(Instruction[6:0]), .b(7'b1101111), .eq(comparator_23_eq));  // open: gt, lt
  Comparator #(.mode("unsigned"), .width(7)) comparator_24 (
    .a(Instruction[6:0]), .b(7'b1100111), .eq(comparator_24_eq[0]));  // open: gt, lt
  Comparator #(.mode("unsigned")) comparator_25 (
    .a({Instruction[31:25], comparator_4_eq[0]}), .b(8'h1), .eq(add0));  // open: gt, lt
  Comparator #(.mode("unsigned")) comparator_26 (
    .a({Instruction[31:25], comparator_4_eq[0]}), .b(8'h3), .eq(mul1));  // open: gt, lt
  Comparator #(.mode("unsigned")) comparator_27 (
    .a({Instruction[31:25], comparator_4_eq[0]}), .b(8'h41), .eq(sub2));  // open: gt, lt
  Comparator #(.mode("unsigned")) comparator_28 (
    .a({Instruction[31:25], comparator_5_eq[0]}), .b(8'h1), .eq(sll3));  // open: gt, lt
  Comparator #(.mode("unsigned")) comparator_29 (
    .a({Instruction[31:25], comparator_5_eq[0]}), .b(8'h3), .eq(mulh4));  // open: gt, lt
  Comparator #(.mode("unsigned")) comparator_30 (
    .a({Instruction[31:25], comparator_19_eq[0]}), .b(8'h1), .eq(srli19));  // open: gt, lt
  Comparator #(.mode("unsigned")) comparator_31 (
    .a({Instruction[31:25], comparator_19_eq[0]}), .b(8'h41), .eq(srai20));  // open: gt, lt
  Comparator #(.mode("unsigned")) comparator_32 (
    .a({Instruction[31:25], comparator_9_eq[0]}), .b(8'h1), .eq(srl8));  // open: gt, lt
  Comparator #(.mode("unsigned")) comparator_33 (
    .a({Instruction[31:25], comparator_9_eq[0]}), .b(8'h41), .eq(sra9));  // open: gt, lt
  Comparator #(.mode("unsigned"), .width(4)) comparator_34 (
    .a({Instruction[14:12], comparator_24_eq[0]}), .b(4'b0001), .eq(comparator_34_eq));  // open: gt, lt
  Comparator #(.mode("unsigned"), .width(4)) comparator_35 (
    .a({Instruction[14:12], comparator_22_eq[0]}), .b(4'b0001), .eq(comparator_35_eq));  // open: gt, lt
  Comparator #(.mode("unsigned"), .width(4)) comparator_36 (
    .a({Instruction[14:12], comparator_22_eq[0]}), .b(4'b0011), .eq(comparator_36_eq));  // open: gt, lt
  Comparator #(.mode("unsigned"), .width(4)) comparator_37 (
    .a({Instruction[14:12], comparator_22_eq[0]}), .b(4'b1001), .eq(comparator_37_eq));  // open: gt, lt
  Comparator #(.mode("unsigned"), .width(4)) comparator_38 (
    .a({Instruction[14:12], comparator_22_eq[0]}), .b(4'b1011), .eq(comparator_38_eq));  // open: gt, lt
  Comparator #(.mode("unsigned"), .width(4)) comparator_39 (
    .a({Instruction[14:12], comparator_22_eq[0]}), .b(4'b1101), .eq(comparator_39_eq));  // open: gt, lt
  Comparator #(.mode("unsigned"), .width(4)) comparator_40 (
    .a({Instruction[14:12], comparator_22_eq[0]}), .b(4'b1111), .eq(comparator_40_eq));  // open: gt, lt
  Comparator #(.mode("unsigned"), .width(7)) comparator_41 (
    .a(Instruction[6:0]), .b(7'b0100011), .eq(comparator_41_eq[0]));  // open: gt, lt
  Comparator #(.mode("unsigned"), .width(7)) comparator_42 (
    .a(Instruction[6:0]), .b(7'b1100011), .eq(comparator_42_eq[0]));  // open: gt, lt
  Comparator #(.mode("unsigned"), .width(7)) comparator_43 (
    .a(Instruction[6:0]), .b(7'b0010111), .eq(auipc32));  // open: gt, lt
  Comparator #(.mode("unsigned"), .width(7)) comparator_44 (
    .a(Instruction[6:0]), .b(7'b0110111), .eq(lui33));  // open: gt, lt
  Comparator #(.mode("unsigned"), .width(7)) comparator_45 (
    .a(Instruction[6:0]), .b(7'b1101111), .eq(jal34));  // open: gt, lt
  Comparator #(.mode("unsigned"), .width(7)) comparator_46 (
    .a(Instruction[6:0]), .b(7'b1100111), .eq(comparator_46_eq[0]));  // open: gt, lt
  not not_1 (not_1_out, BrEq);
  not not_2 (not_2_out, BrLt);
  not not_3 (not_3_out, BrLt);
  and and_1 (and_1_out, BrEq, comparator_35_eq);
  and and_2 (and_2_out, not_1_out, comparator_36_eq);
  and and_3 (and_3_out, BrLt, comparator_37_eq);
  and and_4 (and_4_out, not_2_out, comparator_38_eq);
  and and_5 (and_5_out, BrLt, comparator_39_eq);
  and and_6 (and_6_out, not_3_out, comparator_40_eq);
  Comparator #(.mode("unsigned"), .width(4)) comparator_47 (
    .a({Instruction[14:12], comparator_41_eq[0]}), .b(4'b0001), .eq(sb23));  // open: gt, lt
  Comparator #(.mode("unsigned"), .width(4)) comparator_48 (
    .a({Instruction[14:12], comparator_41_eq[0]}), .b(4'b0011), .eq(sh24));  // open: gt, lt
  Comparator #(.mode("unsigned"), .width(4)) comparator_49 (
    .a({Instruction[14:12], comparator_41_eq[0]}), .b(4'b0101), .eq(sw25));  // open: gt, lt
  Comparator #(.mode("unsigned"), .width(4)) comparator_50 (
    .a({Instruction[14:12], comparator_46_eq[0]}), .b(4'b0001), .eq(jalr35));  // open: gt, lt
  Comparator #(.mode("unsigned"), .width(4)) comparator_51 (
    .a({Instruction[14:12], comparator_42_eq[0]}), .b(4'b0001), .eq(beq26));  // open: gt, lt
  Comparator #(.mode("unsigned"), .width(4)) comparator_52 (
    .a({Instruction[14:12], comparator_42_eq[0]}), .b(4'b0011), .eq(bne27));  // open: gt, lt
  Comparator #(.mode("unsigned"), .width(4)) comparator_53 (
    .a({Instruction[14:12], comparator_42_eq[0]}), .b(4'b1001), .eq(blt28));  // open: gt, lt
  Comparator #(.mode("unsigned"), .width(4)) comparator_54 (
    .a({Instruction[14:12], comparator_42_eq[0]}), .b(4'b1011), .eq(bge29));  // open: gt, lt
  Comparator #(.mode("unsigned"), .width(4)) comparator_55 (
    .a({Instruction[14:12], comparator_42_eq[0]}), .b(4'b1101), .eq(bltu30));  // open: gt, lt
  Comparator #(.mode("unsigned"), .width(4)) comparator_56 (
    .a({Instruction[14:12], comparator_42_eq[0]}), .b(4'b1111), .eq(bgeu31));  // open: gt, lt
  or or_1 (PCSel, and_1_out, and_2_out, and_3_out, and_4_out, and_5_out, and_6_out, comparator_23_eq, comparator_34_eq);
  Priority_Encoder #(.select_enc(6)) priority_encoder_1 (
    .in0(add0), .in1(mul1), .in2(sub2), .in3(sll3), .in4(mulh4), .in5(mulhu5), .in6(slt6), .in7(XOR7),
    .in8(srl8), .in9(sra9), .in10(or10), .in11(and11), .in12(lb12), .in13(lh13), .in14(lw14), .in15(addi15),
    .in16(slli16), .in17(slti17), .in18(xori18), .in19(srli19), .in20(srai20), .in21(ori21), .in22(andi22),
    .in23(sb23), .in24(sh24), .in25(sw25), .in26(beq26), .in27(bne27), .in28(blt28), .in29(bge29),
    .in30(bltu30), .in31(bgeu31), .in32(auipc32), .in33(lui33), .in34(jal34), .in35(jalr35), .out(Address));  // open: in36, in37, in38, in39, in40, in41, in42, in43, in44, in45, in46, in47, in48, in49, in50, in51, in52, in53, in54, in55, in56, in57, in58, in59, in60, in61, in62, in63, gs, en_out, en_in

  // Other names for the same wires on the sheet: Funct7[6:0] = Instruction[31:25]; Funct3[2:0] = Instruction[14:12];
  //   OPcode[6:0] = Instruction[6:0]

  // Notes on the sheet:
  //   INPUTS to your circuit
  //   contents of rom_1 (hex, n*v repeats v):
  //   1007 1407 1607 1087 1487 1587 1107 1207 1287 1687 1307 1387 41 41 41 1041 10c1 1141 1241 12c1 16c1
  //   1341 13c1 3842 3842 3842 4*3064 3074 3074 1067 1067 2069 2041
  //   ROM FOR CONTROL LOGIC
  //   DON'T CHANGE THE LOCATIONS OF THE INPUTS AND OUTPUTS!
  //   This is only if you choose to do the ROM option
  //   OUTPUT from your circuit
  //   Reminder: If using ROM, use combinational logic for PCSel
  //   jal
  //   jalr
  //   blt28
  //   bge29
  //   bltu30
  //   bgeu31
  //   beq26
  //   bne27
endmodule
