// Logisim project partial-load.circ as structural Verilog: 1 circuit, main circuit partial_load
module partial_load (
  input  [31:0] Instruction,
  input  [31:0] MemAddress,
  input  [31:0] DataFromMem,
  output [31:0] DataToReg
);

  wire [31:0] lb01, lb02, lb03, lb04, lh01, lh02, lh03;

  assign lb01 = {{24{DataFromMem[7]}}, DataFromMem[7:0]};  // Bit_Extender bit_extender_1
  assign lb02 = {{24{DataFromMem[15]}}, DataFromMem[15:8]};  // Bit_Extender bit_extender_2
  assign lb03 = {{24{DataFromMem[23]}}, DataFromMem[23:16]};  // Bit_Extender bit_extender_3
  assign lb04 = {{24{DataFromMem[31]}}, DataFromMem[31:24]};  // Bit_Extender bit_extender_4
  assign lh01 = {{16{DataFromMem[15]}}, DataFromMem[15:0]};  // Bit_Extender bit_extender_5
  assign lh03 = {{16{DataFromMem[31]}}, DataFromMem[31:16]};  // Bit_Extender bit_extender_6
  assign lh02 = {{16{DataFromMem[23]}}, DataFromMem[23:8]};  // Bit_Extender bit_extender_7
  Multiplexer #(.select(4), .width(32)) multiplexer_1 (
    .in0(lb01), .in1(lb02), .in2(lb03), .in3(lb04), .in4(lh01), .in5(lh02), .in6(lh03), .in8(DataFromMem),
    .out(DataToReg), .sel({Instruction[13:12], MemAddress[1:0]}));  // open: in7, in9, in10, in11, in12, in13, in14, in15

  // Other names for the same wires on the sheet: MulIndex[3:0] = {Instruction[13:12], MemAddress[1:0]};
  //   Funct2[1:0] = Instruction[13:12]

  // Notes on the sheet:
  //   INPUTS to your circuit
  //   DON'T CHANGE THE LOCATIONS OF THE INPUTS AND OUTPUTS!
  //   OUTPUT from your circuit
endmodule
