// Logisim project partial-store.circ as structural Verilog: 1 circuit, main circuit partial_store
module partial_store (
  input  [31:0] Instruction,
  input  [31:0] MemAddress,
  input  [31:0] DataFromReg,
  input  MemWEn,
  output [3:0] MemWriteMask,
  output [31:0] DataToMem
);

  wire [3:0] bit_extender_3_out, multiplexer_2_out;
  wire [31:0] sb1, sh1;

  assign sb1 = {{24{1'b0}}, DataFromReg[7:0]};  // Bit_Extender bit_extender_1
  assign sh1 = {{16{1'b0}}, DataFromReg[15:0]};  // Bit_Extender bit_extender_2
  Multiplexer #(.select(4), .width(32)) multiplexer_1 (
    .in0(sb1), .in1({{16{1'b0}}, DataFromReg[7:0], {8{1'b0}}}),
    .in2({{8{1'b0}}, DataFromReg[7:0], {16{1'b0}}}), .in3({DataFromReg[7:0], {24{1'b0}}}), .in4(sh1),
    .in6({DataFromReg[15:0], {16{1'b0}}}), .in8(DataFromReg), .out(DataToMem),
    .sel({Instruction[13:12], MemAddress[1:0]}));  // open: in5, in7, in9, in10, in11, in12, in13, in14, in15
  Multiplexer #(.select(4), .width(4)) multiplexer_2 (
    .in0(4'b0001), .in1(4'b0010), .in2(4'b0100), .in3(4'b1000), .in4(4'b0011), .in5(4'b0000), .in6(4'b1100),
    .in7(4'b0000), .in8(4'b1111), .in9(4'b0000), .in10(4'b0000), .in11(4'b0000), .in12(4'b0000),
    .in13(4'b0000), .in14(4'b0000), .in15(4'b0000), .out(multiplexer_2_out),
    .sel({Instruction[13:12], MemAddress[1:0]}));
  assign bit_extender_3_out = {{3{1'b0}}, MemWEn};  // Bit_Extender bit_extender_3
  Multiplier #(.width(4)) multiplier_1 (
    .a(multiplexer_2_out), .b(bit_extender_3_out), .out(MemWriteMask));  // open: cin, cout

  // Other names for the same wires on the sheet: MulIndexs[3:0] = {Instruction[13:12], MemAddress[1:0]};
  //   Funct2s[1:0] = Instruction[13:12]; sb2[15:8] = DataFromReg[7:0]; sb3[23:16] = DataFromReg[7:0];
  //   sb4[31:24] = DataFromReg[7:0]; sh2[31:16] = DataFromReg[15:0]

  // Notes on the sheet:
  //   INPUTS to your circuit
  //   DON'T CHANGE THE LOCATIONS OF THE INPUTS AND OUTPUTS!
  //   OUTPUT from your circuit
endmodule
