// Logisim project R_Type_Test.circ as structural Verilog: 1 circuit, main circuit run_main
module run_main (
  output [31:0] ra,
  output [31:0] sp,
  output [31:0] t0,
  output [31:0] t1,
  output [31:0] t2,
  output [31:0] s0,
  output [31:0] s1,
  output [31:0] a0,
  output [31:0] RequestedAddress,
  output [31:0] RequestedInstruction,
  output [15:0] TimeStep,
  output halt
);

  wire clk;

  Clock clock_1 (.out(clk));
  // Probe on RequestedAddress
  // cpu_harness cpu_harness_1: pin names not known; wires that end beside it: RequestedInstruction, clk, RequestedAddress, ra, sp, t0, t1, t2, s0, s1, a0
  ROM #(.addrWidth(14), .dataWidth(32)) rom_1 (.addr(RequestedAddress[15:2]), .data(RequestedInstruction));
  // Probe on RequestedInstruction
  Counter #(.max('hffff), .width(16)) counter_1 (.clk(clk), .Q(TimeStep));  // open: clr, load, up, count, D, carry
  Comparator #(.width(16)) comparator_1 (.a(TimeStep), .b(16'h11), .eq(halt));  // open: gt, lt

  // Other names for the same wires on the sheet: Instruction[31:0] = RequestedInstruction;
  //   ProgramCounter[31:0] = RequestedAddress

  // Notes on the sheet:
  //   contents of rom_1 (hex, n*v repeats v):
  //   300293 528333 2530333 40530333 5313b3 10000393 27383b3 273b333 2739333 534333 535333 40535333 53e333
  //   53f333 532333
  //   Instruction Memory
  //   Halts Execution After Constant # of Clock Cycles
  //   Constant
endmodule
